# Fritzing sketch Mecanum Wheel RC Car (saved by Fritzing 0.9.3b)
breadboards: 1

parts:
  Part1 = Arduino Pro Mini v13
  U1 = L298_BRIDGE_DRIVER [package=powerso20]
  M1 = DC Motor
  M2 = DC Motor
  M3 = DC Motor
  M4 = DC Motor
  U2 = LIPO-2000mAh [package=lipo-2000]
  U3 = L298_BRIDGE_DRIVER [package=powerso20]

nets:
  N1: Part1.D13/SCK, U3.INC
  N2: Part1.D12/MISO, U3.INA
  N3: Part1.D11_PWM/MOSI, U3.INB
  N4: Part1.D10_PWM/SS, U3.ENA
  N5: Part1.D9_PWM, U1.ENA, U1.ENB
  N6: Part1.D8, U1.INC
  N7: Part1.D7, U1.5V, U1.IND
  N8: Part1.D6_PWM, U1.INB
  N9: Part1.D5_PWM, U1.INA
  N10: Part1.D4, U3.IND
  N11: U1.OUT_A, M2.pin_2
  N12: U1.OUT_B, M2.pin_1
  N13: U1.OUT_D, M1.pin_2
  N14: U1.OUTC, M1.pin_1
  VCC: U1.VCC, U2.+, U3.VCC
  GND: U1.GND, U2.-, U3.GND
  N15: M3.pin_1, U3.OUTC
  N16: M3.pin_2, U3.OUT_D
  N17: M4.pin_1, U3.OUT_B
  N18: M4.pin_2, U3.OUT_A

notes:
  11.7V
  3S Battery

custom parts:
  L298_BRIDGE_DRIVER: Full-bridge power driver IC
